# Fritzing sketch Arduino_wiring (saved by Fritzing 0.9.1b)
breadboards: 1

parts:
  Part1 = Arduino Uno (Rev3) - ICSP
  Part2 = Assembled uBLOX MAX-6 Pico Breakout with Chip Scale Antenna
  U1 = HMC6343 [package=lcc36]
  R1 = Resistor [tolerance=±5% resistance=220 package=THT]
  LED1 = LED - 5mm [color="Red (633nm)" package="5 mm [THT]"]

nets:
  N1: Part1.A4/SDA, U1.SDA
  N2: Part1.A5/SCL, U1.SCL
  N3: Part1.ICSP_MISO, Part1.D12/MISO, R1.Pin_1
  N4: Part1.D4, Part2.RXD
  N5: Part1.D5_PWM, Part2.TXD
  5V: Part1.5V, Part2.VCC, U1.VDD
  GND: Part1.GND, Part2.GND, U1.GND
  N6: R1.Pin_0, LED1.anode

custom parts:
  Assembled uBLOX MAX-6 Pico Breakout with Chip Scale Antenna: The board is assembled with a uBLOX MAX-6 module, chip scale antenna and a decoupling capacitor. This board has VCC, GND and RX & TX, SCL & SDA for I2C. MAX comes in an ultra-compact, easy-to-mount 9.7mm x 10.1mm LCC package, and supports temperatures down to -40'C. Supports temperatures down to -40'C UART interface. RTC crystal for faster warm and hot starts Suitable for HAB Usage Max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
