# Fritzing sketch Untitled Sketch 4 (saved by Fritzing 0.9.1b)
breadboards: 1

parts:
  Part3 = Arduino Uno (Rev3) - ICSP
  U2 = HMC6343 [package=lcc36]

nets:
  N1: Part3.A4/SDA, U2.SDA
  N2: Part3.A5/SCL, U2.SCL
  5V: Part3.5V, U2.VDD
  GND: Part3.GND, U2.GND
